# Fritzing sketch Halloween 2016 (saved by Fritzing 0.9.3b)
circuit board: 8.46667cm x 5.64444cm
breadboards: 1

parts:
  Part1 = Arduino Uno (Rev3)
  BAT1 = BC9VPC [package=bc9vpc]
  R1 = Resistor [tolerance=±5% resistance=220 package=THT]
  R2 = Resistor [tolerance=±5% resistance=220 package=THT]
  LED1 = LED - 5mm [color="Red (633nm)" package="5 mm [THT]"]
  LED2 = LED - 5mm [color="Red (633nm)" package="5 mm [THT]"]
  Part3 = Audio FX Sound Board
  S1 = Pushbutton [package=THT]
  S2 = Pushbutton [package=THT]

nets:
  GND: Part1.GND, BAT1.V-, R1.Pin_1, R2.Pin_1, Part3.GND, S1.leg0, S2.leg0
  N1: Part1.D2, LED2.anode
  N2: Part1.D3_PWM, LED1.anode
  N3: Part1.D4, Part3.0
  N4: Part1.D5_PWM, Part3.1
  N5: Part1.D6_PWM, Part3.2
  N6: Part1.D7, Part3.3
  5V: Part1.5V, Part3.VIN
  N7: Part1.VIN, BAT1.V+
  N8: R1.Pin_0, LED1.cathode
  N9: R2.Pin_0, LED2.cathode
  N10: Part3.VOL+, S1.leg1
  N11: Part3.VOL-, S2.leg1

custom parts:
  Audio FX Sound Board: The Adafruit Sound Board, the fastest way to add audio effects to a project!
